// Logisim project SD_Group07.circ as structural Verilog: 7 circuits, main circuit main
module main (
  output [11:0] pc,
  output [11:0] r0,
  output [11:0] r1,
  output [11:0] r2,
  output [11:0] r3,
  output [11:0] r4,
  output [11:0] r5,
  output [11:0] r6,
  output [11:0] r7,
  output halt
);

  wire and_1_out, clock_1_out, control_logic_1_alu_source, control_logic_1_branch, control_logic_1_jal,
       control_logic_1_jump, control_logic_1_memread, control_logic_1_memtoreg, control_logic_1_memwrite,
       control_logic_1_regwrite, jump_unit_1_branch_absolute, jump_unit_1_branch_relative, not_1_out,
       reset_out;
  wire [2:0] control_logic_1_rd, control_logic_1_rs, control_logic_1_rt;
  wire [3:0] control_logic_1_alu;
  wire [11:0] immediate_logic_1_out_2, jump_unit_1_branch_value, multiplexer_1_out, multiplexer_2_out,
       multiplexer_3_out, n12_bit_alu_1_result, program_counter_1_out_7, ram_2_data, undriven, undriven_2;
  wire [12:0] ram_1_data;

  Halt halt_1 (.instruction(ram_1_data), .clock(clock_1_out), .reset(reset_out), .halt(halt));
  Clock clock_1 (.out(clock_1_out));
  Button reset (.out(reset_out));
  and and_1 (and_1_out, ~halt, clock_1_out);  // AND_Gate
  program_counter program_counter_1 (
    .Branch_relative(jump_unit_1_branch_relative), .Branch_absolute(jump_unit_1_branch_absolute),
    .Branch_value(jump_unit_1_branch_value), .C(and_1_out), .Reset(reset_out), .out_6(pc),
    .out_7(program_counter_1_out_7));
  Control_Logic control_logic_1 (
    .in_1(ram_1_data), .RegWrite(control_logic_1_regwrite), .MemToReg(control_logic_1_memtoreg),
    .MemWrite(control_logic_1_memwrite), .MemRead(control_logic_1_memread), .ALU(control_logic_1_alu),
    .ALU_Source(control_logic_1_alu_source), .Rt(control_logic_1_rt), .Rd(control_logic_1_rd),
    .Rs(control_logic_1_rs), .Jump(control_logic_1_jump), .Branch(control_logic_1_branch),
    .Jal(control_logic_1_jal));
  RAM #(.addrWidth(12), .dataWidth(13)) ram_1 (
    .addr(pc), .data(ram_1_data), .sel(1'b1), .clk(and_1_out), .ld(1'b1), .clr(reset_out));
  Immediate_Logic immediate_logic_1 (.in_1(ram_1_data), .out_2(immediate_logic_1_out_2));
  Multiplexer #(.width(12), .enable("false")) multiplexer_1 (
    .in0(multiplexer_3_out), .in1(program_counter_1_out_7), .out(multiplexer_1_out), .sel(control_logic_1_jal));
  Jump_Unit jump_unit_1 (
    .Jump(control_logic_1_jump), .Branch(control_logic_1_branch), .ALU_Out(n12_bit_alu_1_result),
    .Immediate(immediate_logic_1_out_2), .Branch_Relative(jump_unit_1_branch_relative),
    .Branch_Absolute(jump_unit_1_branch_absolute), .Branch_Value(jump_unit_1_branch_value));
  // register_file register_file_1: pin names not known; wires that end beside it: control_logic_1_rt, and_1_out, control_logic_1_rs, control_logic_1_rd, multiplexer_1_out, control_logic_1_regwrite, reset_out
  _12_bit_ALU u_12_bit_alu_1 (
    .ALU_code(control_logic_1_alu), .a(undriven), .b(multiplexer_2_out), .result(n12_bit_alu_1_result));  // open: overflow
  Multiplexer #(.width(12), .enable("false")) multiplexer_2 (
    .in0(undriven_2), .in1(immediate_logic_1_out_2), .out(multiplexer_2_out), .sel(control_logic_1_alu_source));
  RAM #(.addrWidth(12), .dataWidth(12), .bus("separate")) ram_2 (
    .addr(n12_bit_alu_1_result), .din(undriven_2), .data(ram_2_data), .str(control_logic_1_memwrite),
    .sel(1'b1), .clk(and_1_out), .ld(control_logic_1_memread), .clr(reset_out));
  not not_1 (not_1_out, control_logic_1_memtoreg);
  Multiplexer #(.width(12), .enable("false")) multiplexer_3 (
    .in0(ram_2_data), .in1(n12_bit_alu_1_result), .out(multiplexer_3_out), .sel(not_1_out));

  // Notes on the sheet:
  //   current instruction
  //   clock signal
  //   reset button
  //   RegWrite
  //   DO NOT CHANGE THE INPUTS AND OUTPUTS OF THIS CIRCUIT! Do not add/remove inputs or outputs. Do not even change their location or orientation.
  //   MemToReg
  //   Memread
  //   Memwrite
endmodule

module Halt (
  input  [12:0] instruction,
  input  clock,
  input  reset,
  output halt
);

  wire and_1_out, comparator_1_eq, comparator_2_gt, counter_1_carry, or_1_out, or_2_out;
  wire [11:0] counter_1_q;

  Comparator #(.width(13), .mode("unsigned")) comparator_1 (
    .a(instruction), .b({13{1'b0}}), .eq(comparator_1_eq));  // open: gt, lt
  Counter #(.width(12), .max('hfff), .trigger("falling")) counter_1 (
    .Q(counter_1_q), .carry(counter_1_carry), .clk(clock), .clr(reset));  // open: load, D, count
  or or_1 (or_1_out, comparator_1_eq, counter_1_carry);
  Comparator #(.width(12), .mode("unsigned")) comparator_2 (
    .a(counter_1_q), .b({12{1'b0}}), .gt(comparator_2_gt));  // open: eq, lt
  or or_2 (or_2_out, halt, and_1_out);
  and and_1 (and_1_out, or_1_out, comparator_2_gt);
  Register #(.width(1)) register_1 (.D(or_2_out), .Q(halt), .clk(clock), .clr(reset));  // open: en

  // Notes on the sheet:
  //   halt becomes and stays asserted if the instruction is 0000 (not in the first clock cycle) or the end of the counter is reached (2^12)
endmodule

module program_counter (
  input  Branch_relative,
  input  Branch_absolute,
  input  [11:0] Branch_value,
  input  C,
  input  Reset,
  output [11:0] out_6,
  output [11:0] out_7
);

  wire and_1_out;
  wire [1:0] priority_encoder_1_out;
  wire [11:0] multiplexer_1_out, n12bit_cla_1_out_4;

  _12bit_CLA u_12bit_cla_1 (
    .in_1(Branch_value), .in_2(out_6), .in_3(1'b0), .out_4(n12bit_cla_1_out_4));  // open: Overflow
  and and_1 (and_1_out, ~Branch_relative, ~Branch_absolute);  // AND_Gate
  Priority_Encoder #(.select(2)) priority_encoder_1 (
    .in0(Branch_relative), .in1(Branch_absolute), .in2(and_1_out), .out(priority_encoder_1_out));  // open: in3, gs, en_out, en_in
  Multiplexer #(.select(2), .width(12), .enable("false")) multiplexer_1 (
    .in0(n12bit_cla_1_out_4), .in1(Branch_value), .in2(out_7), .out(multiplexer_1_out),
    .sel(priority_encoder_1_out));  // open: in3
  _12bit_register u_12bit_register_1 (.Input(multiplexer_1_out), .Reset(Reset), .Write(1'b1), .Clock(C), .out_5(out_6));
  _12bit_CLA u_12bit_cla_2 (.in_1(out_6), .in_2(12'h1), .in_3(1'b0), .out_4(out_7));  // open: Overflow
endmodule

module Control_Logic (
  input  [12:0] in_1,
  output RegWrite,
  output MemToReg,
  output MemWrite,
  output MemRead,
  output [3:0] ALU,
  output ALU_Source,
  output [2:0] Rt,
  output [2:0] Rd,
  output [2:0] Rs,
  output Jump,
  output Branch,
  output Jal
);

  wire and_1_out, and_2_out, and_3_out, and_4_out, and_7_out, and_8_out, and_10_out, and_11_out, and_12_out,
       not_1_out, not_2_out, not_3_out, not_4_out, not_5_out, not_6_out, not_7_out, not_8_out, not_9_out,
       not_10_out, not_11_out, not_12_out, not_13_out, not_14_out, not_15_out, not_16_out, or_1_out,
       or_2_out, or_3_out, or_4_out, or_5_out;
  wire [2:0] multiplexer_8_out;
  wire [3:0] bit_extender_1_out, multiplexer_1_out, multiplexer_2_out, multiplexer_3_out, multiplexer_5_out;

  assign bit_extender_1_out = {{1{1'b1}}, in_1[2:0]};  // Bit_Extender bit_extender_1
  and and_1 (and_1_out, ~in_1[2], ~in_1[1], ~in_1[0], and_2_out);  // AND_Gate
  Multiplexer #(.width(4), .enable("false")) multiplexer_1 (
    .in0(bit_extender_1_out), .in1(4'b0000), .out(multiplexer_1_out), .sel(and_1_out));
  not not_1 (not_1_out, in_1[9]);
  not not_2 (not_2_out, in_1[10]);
  not not_3 (not_3_out, in_1[11]);
  not not_4 (not_4_out, in_1[12]);
  and and_2 (and_2_out, not_1_out, not_2_out, not_3_out, not_4_out);
  and and_3 (and_3_out, ~and_1_out, and_2_out);  // AND_Gate
  and and_4 (and_4_out, ~and_2_out, ~or_1_out);  // AND_Gate
  not not_5 (not_5_out, and_4_out);
  Multiplexer #(.width(4), .enable("false")) multiplexer_2 (
    .in0(in_1[12:9]), .in1(multiplexer_1_out), .out(multiplexer_2_out), .sel(not_5_out));
  and and_5 (MemRead, in_1[9], not_2_out, not_3_out, in_1[12]);
  or or_1 (or_1_out, and_11_out, and_10_out, Branch, and_8_out, and_7_out, MemWrite, MemRead);
  and and_6 (MemWrite, not_1_out, in_1[10], not_3_out, in_1[12]);
  not not_6 (not_6_out, MemWrite);
  not not_7 (not_7_out, MemRead);
  not not_8 (not_8_out, and_4_out);
  not not_9 (not_9_out, and_3_out);
  not not_10 (not_10_out, and_1_out);
  and and_7 (and_7_out, in_1[12], not_3_out, in_1[10], in_1[9]);
  and and_8 (and_8_out, in_1[12], in_1[11], not_2_out, not_1_out);
  and and_9 (Branch, in_1[12], in_1[11], not_2_out, in_1[9]);
  and and_10 (and_10_out, in_1[12], in_1[11], in_1[10], not_1_out);
  and and_11 (and_11_out, in_1[9], in_1[10], in_1[11], in_1[12]);
  not not_11 (not_11_out, and_11_out);
  not not_12 (not_12_out, and_10_out);
  not not_13 (not_13_out, Branch);
  not not_14 (not_14_out, and_8_out);
  not not_15 (not_15_out, and_7_out);
  or or_2 (or_2_out, MemRead, MemWrite);
  or or_3 (or_3_out, and_7_out, and_8_out, and_10_out, and_11_out);
  Multiplexer #(.width(4), .enable("false")) multiplexer_3 (
    .in0(multiplexer_2_out), .in1(4'b0011), .out(multiplexer_3_out), .sel(or_2_out));
  Multiplexer #(.width(3), .enable("false")) multiplexer_4 (.in0(in_1[2:0]), .in1(in_1[8:6]), .out(Rt), .sel(MemWrite));
  Multiplexer #(.width(4), .enable("false")) multiplexer_5 (
    .in0(multiplexer_3_out), .in1(4'b0001), .out(multiplexer_5_out), .sel(or_3_out));
  nor nor_1 (RegWrite, and_12_out, MemWrite, Branch, and_10_out);
  and and_12 (and_12_out, and_11_out, ~Jal);  // AND_Gate
  or or_4 (or_4_out, Branch, and_10_out, and_11_out);
  Multiplexer #(.width(4), .enable("false")) multiplexer_6 (
    .in0(multiplexer_5_out), .in1(4'b1111), .out(ALU), .sel(or_4_out));
  and and_13 (Jal, in_1[0], and_11_out);
  Multiplexer #(.width(3), .enable("false")) multiplexer_7 (.in0(in_1[8:6]), .in1(3'b111), .out(Rd), .sel(Jal));
  or or_5 (or_5_out, and_10_out, Branch, and_7_out);
  not not_16 (not_16_out, or_5_out);
  Multiplexer #(.width(3), .enable("false")) multiplexer_8 (
    .in0(in_1[8:6]), .in1(in_1[5:3]), .out(multiplexer_8_out), .sel(not_16_out));
  or or_6 (ALU_Source, MemWrite, and_7_out, MemRead, and_8_out);
  Multiplexer #(.width(3), .enable("false")) multiplexer_9 (
    .in0(multiplexer_8_out), .in1(3'b000), .out(Rs), .sel(and_8_out));
  or or_7 (Jump, and_11_out, and_10_out);

  assign MemToReg = MemRead;

  // Notes on the sheet:
  //   Zero
  //   Unary
  //   Binary
  //   Lw
  //   Sw
  //   Ori
  //   Lui
  //   brnz
  //   jr
  //   j
endmodule

module Immediate_Logic (
  input  [12:0] in_1,
  output [11:0] out_2
);

  wire and_1_out, and_2_out, and_3_out, and_4_out, and_5_out, and_6_out, and_7_out, not_1_out, not_2_out,
       not_3_out, not_4_out, or_1_out, or_2_out, or_3_out;
  wire [11:0] bit_extender_1_out, bit_extender_2_out, bit_extender_3_out, bit_extender_4_out,
       multiplexer_1_out, multiplexer_2_out, multiplexer_3_out, multiplexer_4_out;

  not not_1 (not_1_out, in_1[9]);
  not not_2 (not_2_out, in_1[10]);
  not not_3 (not_3_out, in_1[11]);
  not not_4 (not_4_out, in_1[12]);
  assign bit_extender_1_out = {{9{1'b0}}, in_1[2:0]};  // Bit_Extender bit_extender_1
  assign bit_extender_2_out = {{6{1'b0}}, in_1[5:0]};  // Bit_Extender bit_extender_2
  assign bit_extender_3_out = {{6{in_1[5]}}, in_1[5:0]};  // Bit_Extender bit_extender_3
  assign bit_extender_4_out = {{4{1'b0}}, in_1[8:1]};  // Bit_Extender bit_extender_4
  and and_1 (and_1_out, in_1[9], not_2_out, not_3_out, in_1[12]);
  or or_1 (or_1_out, and_1_out, and_2_out);
  Multiplexer #(.width(12), .enable("false")) multiplexer_1 (
    .in0({12{1'b0}}), .in1(bit_extender_1_out), .out(multiplexer_1_out), .sel(or_1_out));
  and and_2 (and_2_out, not_1_out, in_1[10], not_3_out, in_1[12]);
  Multiplexer #(.width(12), .enable("false")) multiplexer_2 (
    .in0(bit_extender_2_out), .in1({in_1[5:0], {6{1'b0}}}), .out(multiplexer_2_out), .sel(and_4_out));
  and and_3 (and_3_out, in_1[12], not_3_out, in_1[10], in_1[9]);
  or or_2 (or_2_out, and_3_out, and_4_out);
  and and_4 (and_4_out, in_1[12], in_1[11], not_2_out, not_1_out);
  Multiplexer #(.width(12), .enable("false")) multiplexer_3 (
    .in0(multiplexer_1_out), .in1(multiplexer_2_out), .out(multiplexer_3_out), .sel(or_2_out));
  and and_5 (and_5_out, in_1[12], in_1[11], not_2_out, in_1[9]);
  or or_3 (or_3_out, and_5_out, and_6_out);
  and and_6 (and_6_out, in_1[12], in_1[11], in_1[10], not_1_out);
  Multiplexer #(.width(12), .enable("false")) multiplexer_4 (
    .in0(multiplexer_3_out), .in1(bit_extender_3_out), .out(multiplexer_4_out), .sel(or_3_out));
  and and_7 (and_7_out, in_1[9], in_1[10], in_1[11], in_1[12]);
  Multiplexer #(.width(12), .enable("false")) multiplexer_5 (
    .in0(multiplexer_4_out), .in1(bit_extender_4_out), .out(out_2), .sel(and_7_out));

  // Notes on the sheet:
  //   Lw
  //   Sw
  //   Ori
  //   Lui
  //   brnz
  //   jr
  //   j
endmodule

module Jump_Unit (
  input  Jump,
  input  Branch,
  input  [11:0] ALU_Out,
  input  [11:0] Immediate,
  output Branch_Relative,
  output Branch_Absolute,
  output [11:0] Branch_Value
);

  wire not_1_out, zero_1_out_2;
  wire [11:0] n12bit_cla_1_out_4, n12bit_cla_2_out_4;

  Zero zero_1 (.in_1(ALU_Out), .out_2(zero_1_out_2));
  not not_1 (not_1_out, zero_1_out_2);
  and and_1 (Branch_Relative, not_1_out, Branch);
  _12bit_CLA u_12bit_cla_1 (
    .in_1(ALU_Out), .in_2(Immediate), .in_3(1'b0), .out_4(n12bit_cla_1_out_4));  // open: Overflow
  _12bit_CLA u_12bit_cla_2 (.in_1(Immediate), .in_2(12'h1), .in_3(1'b0), .out_4(n12bit_cla_2_out_4));  // open: Overflow
  Multiplexer #(.width(12), .enable("false")) multiplexer_1 (
    .in0(n12bit_cla_1_out_4), .in1(n12bit_cla_2_out_4), .out(Branch_Value), .sel(Branch_Relative));

  assign Branch_Absolute = Jump;
endmodule

module Zero (
  input  [11:0] in_1,
  output out_2
);

  wire or_1_out;

  or or_1 (or_1_out, in_1[11], in_1[10], in_1[9], in_1[8], in_1[7], in_1[6], in_1[4], in_1[3], in_1[2], in_1[1], in_1[0], in_1[5]);
  not not_1 (out_2, or_1_out);
endmodule
