// Logisim project memory.circ as structural Verilog
module _12bit_register (
  input  [11:0] Input,
  input  Reset,
  input  Write,
  input  Clock,
  output [11:0] out_5
);

  wire or_1_out;
  wire [11:0] multiplexer_1_out;

  Multiplexer #(.width(12), .enable("false")) multiplexer_1 (
    .in0(Input), .in1({12{1'b0}}), .out(multiplexer_1_out), .sel(Reset));
  or or_1 (or_1_out, Reset, Write);
  D_Flip_Flop #(.trigger("falling")) d_ff_1 (
    .clk(Clock), .D(multiplexer_1_out[5]), .Q(out_5[5]), .en(or_1_out));  // open: Qn, preset, reset
  D_Flip_Flop #(.trigger("falling")) d_ff_2 (
    .clk(Clock), .D(multiplexer_1_out[11]), .Q(out_5[11]), .en(or_1_out));  // open: Qn, preset, reset
  D_Flip_Flop #(.trigger("falling")) d_ff_3 (
    .clk(Clock), .D(multiplexer_1_out[4]), .Q(out_5[4]), .en(or_1_out));  // open: Qn, preset, reset
  D_Flip_Flop #(.trigger("falling")) d_ff_4 (
    .clk(Clock), .D(multiplexer_1_out[10]), .Q(out_5[10]), .en(or_1_out));  // open: Qn, preset, reset
  D_Flip_Flop #(.trigger("falling")) d_ff_5 (
    .clk(Clock), .D(multiplexer_1_out[3]), .Q(out_5[3]), .en(or_1_out));  // open: Qn, preset, reset
  D_Flip_Flop #(.trigger("falling")) d_ff_6 (
    .clk(Clock), .D(multiplexer_1_out[9]), .Q(out_5[9]), .en(or_1_out));  // open: Qn, preset, reset
  D_Flip_Flop #(.trigger("falling")) d_ff_7 (
    .clk(Clock), .D(multiplexer_1_out[2]), .Q(out_5[2]), .en(or_1_out));  // open: Qn, preset, reset
  D_Flip_Flop #(.trigger("falling")) d_ff_8 (
    .clk(Clock), .D(multiplexer_1_out[8]), .Q(out_5[8]), .en(or_1_out));  // open: Qn, preset, reset
  D_Flip_Flop #(.trigger("falling")) d_ff_9 (
    .clk(Clock), .D(multiplexer_1_out[1]), .Q(out_5[1]), .en(or_1_out));  // open: Qn, preset, reset
  D_Flip_Flop #(.trigger("falling")) d_ff_10 (
    .clk(Clock), .D(multiplexer_1_out[7]), .Q(out_5[7]), .en(or_1_out));  // open: Qn, preset, reset
  D_Flip_Flop #(.trigger("falling")) d_ff_11 (
    .clk(Clock), .D(multiplexer_1_out[0]), .Q(out_5[0]), .en(or_1_out));  // open: Qn, preset, reset
  D_Flip_Flop #(.trigger("falling")) d_ff_12 (
    .clk(Clock), .D(multiplexer_1_out[6]), .Q(out_5[6]), .en(or_1_out));  // open: Qn, preset, reset
endmodule

module register_file (
  input  [2:0] rs,
  input  [2:0] rt,
  input  [2:0] rd,
  input  [11:0] data,
  input  write,
  input  clock,
  input  reset,
  output [11:0] S,
  output [11:0] T
);

  wire and_1_out, and_2_out, and_3_out, and_4_out, and_5_out, and_6_out, and_7_out, and_8_out,
       decoder_1_out0, decoder_1_out1, decoder_1_out2, decoder_1_out3, decoder_1_out4, decoder_1_out5,
       decoder_1_out6, decoder_1_out7;
  wire [11:0] n12bit_register_1_out_5, n12bit_register_2_out_5, n12bit_register_3_out_5,
       n12bit_register_4_out_5, n12bit_register_5_out_5, n12bit_register_6_out_5, n12bit_register_7_out_5,
       n12bit_register_8_out_5;

  Decoder #(.select(3), .enable("false")) decoder_1 (
    .out0(decoder_1_out0), .out1(decoder_1_out1), .out2(decoder_1_out2), .out3(decoder_1_out3),
    .out4(decoder_1_out4), .out5(decoder_1_out5), .out6(decoder_1_out6), .out7(decoder_1_out7), .sel(rd));
  and and_1 (and_1_out, write, decoder_1_out0);
  and and_2 (and_2_out, write, decoder_1_out1);
  and and_3 (and_3_out, write, decoder_1_out2);
  and and_4 (and_4_out, write, decoder_1_out3);
  and and_5 (and_5_out, write, decoder_1_out4);
  and and_6 (and_6_out, write, decoder_1_out5);
  and and_7 (and_7_out, write, decoder_1_out6);
  and and_8 (and_8_out, write, decoder_1_out7);
  _12bit_register u_12bit_register_1 (
    .Input(data), .Reset(reset), .Write(and_1_out), .Clock(clock), .out_5(n12bit_register_1_out_5));
  _12bit_register u_12bit_register_2 (
    .Input(data), .Reset(reset), .Write(and_2_out), .Clock(clock), .out_5(n12bit_register_2_out_5));
  _12bit_register u_12bit_register_3 (
    .Input(data), .Reset(reset), .Write(and_3_out), .Clock(clock), .out_5(n12bit_register_3_out_5));
  _12bit_register u_12bit_register_4 (
    .Input(data), .Reset(reset), .Write(and_4_out), .Clock(clock), .out_5(n12bit_register_4_out_5));
  _12bit_register u_12bit_register_5 (
    .Input(data), .Reset(reset), .Write(and_5_out), .Clock(clock), .out_5(n12bit_register_5_out_5));
  _12bit_register u_12bit_register_6 (
    .Input(data), .Reset(reset), .Write(and_6_out), .Clock(clock), .out_5(n12bit_register_6_out_5));
  _12bit_register u_12bit_register_7 (
    .Input(data), .Reset(reset), .Write(and_7_out), .Clock(clock), .out_5(n12bit_register_7_out_5));
  _12bit_register u_12bit_register_8 (
    .Input(data), .Reset(reset), .Write(and_8_out), .Clock(clock), .out_5(n12bit_register_8_out_5));
  Multiplexer #(.select(3), .width(12), .enable("false")) multiplexer_1 (
    .in0(n12bit_register_1_out_5), .in1(n12bit_register_2_out_5), .in2(n12bit_register_3_out_5),
    .in3(n12bit_register_4_out_5), .in4(n12bit_register_5_out_5), .in5(n12bit_register_6_out_5),
    .in6(n12bit_register_7_out_5), .in7(n12bit_register_8_out_5), .out(S), .sel(rs));
  Multiplexer #(.select(3), .width(12), .enable("false")) multiplexer_2 (
    .in0(n12bit_register_1_out_5), .in1(n12bit_register_2_out_5), .in2(n12bit_register_3_out_5),
    .in3(n12bit_register_4_out_5), .in4(n12bit_register_5_out_5), .in5(n12bit_register_6_out_5),
    .in6(n12bit_register_7_out_5), .in7(n12bit_register_8_out_5), .out(T), .sel(rt));
endmodule

module counter (
  input  Clock,
  input  [11:0] Data,
  output [11:0] out_3
);

  wire comparator_1_eq, comparator_1_gt, comparator_1_lt, or_1_out;
  wire [11:0] undriven;

  _12bit_register u_12bit_register_1 (
    .Input(undriven), .Reset(or_1_out), .Write(comparator_1_lt), .Clock(Clock), .out_5(out_3));
  _12bit_CLA u_12bit_cla_1 (.in_1(out_3), .in_2(12'h1), .in_3(1'b0));  // open: out_4, Overflow
  or or_1 (or_1_out, comparator_1_gt, comparator_1_eq);
  Comparator #(.width(12)) comparator_1 (
    .a(undriven), .b(Data), .gt(comparator_1_gt), .eq(comparator_1_eq), .lt(comparator_1_lt));
endmodule
